# Fritzing sketch Multiplexing (saved by Fritzing 0.9.3b)
breadboards: 1

parts:
  LED1 = LED - 5mm [color="Red (633nm)" package="5 mm [THT]"]
  LED2 = LED - 5mm [color="Red (633nm)" package="5 mm [THT]"]
  Part1 = Arduino Uno (Rev3)
  LED3 = LED - 5mm [color="Red (633nm)" package="5 mm [THT]"]
  LED4 = LED - 5mm [color="Red (633nm)" package="5 mm [THT]"]
  R2 = Resistor [tolerance=±5% resistance=220 package=THT]
  R3 = Resistor [tolerance=±5% resistance=220 package=THT]
  S1 = Pushbutton [package="[THT]"]
  R4 = Resistor [tolerance=±5% resistance=10k package=THT]

nets:
  N1: LED1.cathode, LED2.cathode, R2.Pin_1
  N2: LED1.anode, Part1.D8, LED3.anode
  N3: LED2.anode, Part1.D9_PWM, LED4.anode
  N4: Part1.D13/SCK, R4.Pin_1
  N5: Part1.D2, R2.Pin_0
  N6: Part1.D3_PWM, R3.Pin_0
  N7: Part1.3V3, S1.Pin_3, S1.Pin_4
  N8: Part1.GND, S1.Pin_1, S1.Pin_2, R4.Pin_0
  N9: LED3.cathode, LED4.cathode

notes:
  Red and Yellow = Row pins
  Blue = Collumn pins
  Green detects circuit closing on on push
